# Fritzing sketch bluetooth-controlled-car (saved by Fritzing 0.8.7b)

parts:
  S1 = H-Bridge with L298N
  M1 = DC Motor
  M2 = DC Motor  # not connected
  S2 = SPST Switch [package=r_sw_th]
  18650_holder2 = 18650 holder [package="DIP (Dual Inline) [THT]"]
  18650_holder3 = 18650 holder [package="DIP (Dual Inline) [THT]"]
  Componente1 = Arduino Nano (Rev3.0)
  TCRT2 = TCRT5000 sensor module [part_number=151608]
  TCRT3 = TCRT5000 sensor module [part_number=151608]
  Componente2 = SRF05 Ultrasonic Rangefinder
  Componente3 = Bluetooth HC-05 Macho
  R1 = Resistor [tolerance=±5% resistance=1k package=THT]  # not connected
  R2 = Resistor [tolerance=±5% resistance=2k package=THT]

nets:
  12V: S1.12V, Componente1.VIN
  N1: S1.IN1, Componente1.D5
  N2: S1.IN2, Componente1.D4
  N3: S1.IN3, Componente1.D3
  N4: S1.IN4, Componente1.D2
  N5: S1.OUT4-Motor2, M1.pin_1
  N6: S2.O, 18650_holder3.holder_+
  N7: 18650_holder2.holder_+, 18650_holder3.holder_-
  N8: Componente1.D0/RX, Componente3.TXD
  N9: Componente1.D10, Componente2.Trig
  N10: Componente1.D11/MOSI, Componente2.Echo
  N11: Componente1.A2, TCRT2.D-
  N12: Componente1.A1, TCRT3.D-
  N13: Componente3.RXD, R2.Pin_0

custom parts:
  H-Bridge with L298N: h-bridge
  18650 holder: Акум формата 18650 в холдере
  TCRT5000 sensor module: breakout board with TCRT5000
