# Fritzing sketch circuito-carro (saved by Fritzing 0.8.7b)

parts:
  Componente1 = Arduino Uno (Rev3)
  S1 = H-Bridge with L298N
  TCRT1 = TCRT5000 sensor module [part_number=151608]
  TCRT2 = TCRT5000 sensor module [part_number=151608]
  Componente2 = Bluetooth HC-05 Macho
  Componente3 = SRF05 Ultrasonic Rangefinder
  M1 = DC Motor
  M2 = DC Motor  # not connected
  S2 = SPST Switch [package=r_sw_th]
  18650_holder1 = 18650 holder [package="DIP (Dual Inline) [THT]"]
  18650_holder2 = 18650 holder [package="DIP (Dual Inline) [THT]"]

nets:
  N1: Componente1.D8, S1.IN4
  N2: Componente1.D10_PWM/SS, Componente3.Trig
  N3: Componente1.D11_PWM/MOSI, Componente3.Echo
  GND: Componente1.GND, Componente2.GND, Componente3.GND
  N4: Componente1.D0/RX, Componente2.TXD
  N5: Componente1.D1/TX, Componente2.RXD
  N6: Componente1.D2, TCRT2.D+
  N7: Componente1.D3_PWM, TCRT1.D+
  N8: Componente1.D4, S1.IN1
  N9: Componente1.D6_PWM, S1.IN2
  N10: Componente1.D7, S1.IN3
  5V: Componente1.5V, Componente3.VCC
  VIN: Componente1.VIN, S1.12V, S2.S
  N11: S1.OUT4-Motor2, M1.pin_1
  N12: S2.P, 18650_holder2.holder_+
  N13: 18650_holder1.holder_+, 18650_holder2.holder_-

custom parts:
  H-Bridge with L298N: h-bridge
  TCRT5000 sensor module: breakout board with TCRT5000
  18650 holder: Акум формата 18650 в холдере
